// Logisim project cpu.circ as structural Verilog: 1 circuit, main circuit cpu
module cpu (
  input  clk,
  input  [31:0] INSTRUCTION,
  input  [31:0] READ_DATA,
  output [31:0] WRITE_ADDRESS,
  output [31:0] PROGRAM_COUNTER,
  output [31:0] ra,
  output [31:0] sp,
  output [31:0] t0,
  output [31:0] t1,
  output [31:0] t2,
  output [31:0] s0,
  output [31:0] s1,
  output [31:0] a0,
  output [31:0] tohost,
  output [3:0] WRITE_ENABLE,
  output [31:0] WRITE_DATA
);

  wire branch_comp_1_breq, branch_comp_1_brlt, control_logic_1_asel, control_logic_1_brun,
       control_logic_1_bsel, control_logic_1_csrsel, control_logic_1_csrwen, control_logic_1_pcsel,
       control_logic_1_regwen;
  wire [1:0] control_logic_1_wbsel;
  wire [2:0] control_logic_1_immsel;
  wire [3:0] control_logic_1_alusel;
  wire [4:0] register_1_q_2, register_1_q_3, register_1_q_4;
  wire [31:0] adder_1_out, imm_gen_1_imm, multiplexer_1_out, multiplexer_2_out, multiplexer_3_out,
       multiplexer_4_out, multiplexer_5_out, multiplexer_6_out, PC_n_4, PC_stored, regfile_1_read_data_1,
       register_1_q;

  Adder #(.width(32)) adder_1 (.a(PROGRAM_COUNTER), .b(32'h4), .out(adder_1_out));  // open: cin, cout
  Multiplexer #(.enable("false"), .width(32)) multiplexer_1 (
    .in0(adder_1_out), .in1(WRITE_ADDRESS), .out(multiplexer_1_out), .sel(control_logic_1_pcsel));
  Multiplexer #(.enable("false"), .width(32)) multiplexer_2 (
    .in0(INSTRUCTION), .in1(32'h13), .out(multiplexer_2_out), .sel(control_logic_1_pcsel));
  Register #(.width(32)) PC (.D(multiplexer_1_out), .en(1'b1), .clk(clk), .Q(PROGRAM_COUNTER));  // open: clr
  Register #(.width(32)) register_1 (
    .D(multiplexer_2_out), .en(1'b1), .clk(clk),
    .Q({register_1_q[31:25], register_1_q_3, register_1_q_2, register_1_q[14:12], register_1_q_4, register_1_q[6:0]}));  // open: clr
  Register #(.width(32)) register_2 (.D(adder_1_out), .en(1'b1), .clk(clk), .Q(PC_n_4));  // open: clr
  Register #(.width(32)) register_3 (.D(PROGRAM_COUNTER), .en(1'b1), .clk(clk), .Q(PC_stored));  // open: clr
  control_logic control_logic_1 (
    .CSRWen(control_logic_1_csrwen), .PCSel(control_logic_1_pcsel), .RegWEn(control_logic_1_regwen),
    .ImmSel(control_logic_1_immsel), .BrUn(control_logic_1_brun), .ASel(control_logic_1_asel),
    .BSel(control_logic_1_bsel), .ALUSel(control_logic_1_alusel), .MemRW(WRITE_ENABLE[3]),
    .WBSel(control_logic_1_wbsel), .CSRSel(control_logic_1_csrsel),
    .inst({register_1_q[31:25], register_1_q_3, register_1_q_2, register_1_q[14:12], register_1_q_4, register_1_q[6:0]}),
    .BrEq(branch_comp_1_breq), .BrLt(branch_comp_1_brlt));
  regfile regfile_1 (
    .rs1(register_1_q_2), .rs2(register_1_q_3), .rd(register_1_q_4), .Write_Data(multiplexer_6_out),
    .RegWEn(control_logic_1_regwen), .clk(clk), .ra(ra), .sp(sp), .t0(t0), .t1(t1), .t2(t2), .s0(s0),
    .s1(s1), .a0(a0), .Read_Data_1(regfile_1_read_data_1), .Read_Data_2(WRITE_DATA));
  imm_gen imm_gen_1 (
    .inst({register_1_q[31:25], register_1_q_3, register_1_q_2, register_1_q[14:12], register_1_q_4, register_1_q[6:0]}),
    .ImmSel(control_logic_1_immsel), .imm(imm_gen_1_imm));
  Multiplexer #(.enable("false"), .width(32)) multiplexer_3 (
    .in0(PC_stored), .in1(regfile_1_read_data_1), .out(multiplexer_3_out), .sel(control_logic_1_asel));
  Multiplexer #(.enable("false"), .width(32)) multiplexer_4 (
    .in0(WRITE_DATA), .in1(imm_gen_1_imm), .out(multiplexer_4_out), .sel(control_logic_1_bsel));
  branch_comp branch_comp_1 (
    .rs1(regfile_1_read_data_1), .rs2(WRITE_DATA), .BrUn(control_logic_1_brun), .BrEq(branch_comp_1_breq),
    .BrLt(branch_comp_1_brlt));
  alu alu_1 (.Result(WRITE_ADDRESS), .A(multiplexer_3_out), .B(multiplexer_4_out), .ALUSel(control_logic_1_alusel));
  Multiplexer #(.enable("false"), .width(32)) multiplexer_5 (
    .in0(imm_gen_1_imm), .in1(regfile_1_read_data_1), .out(multiplexer_5_out), .sel(control_logic_1_csrsel));
  csr csr_1 (
    .CSR_address({register_1_q[31:25], register_1_q_3}), .CSR_din(multiplexer_5_out),
    .CSR_WE(control_logic_1_csrwen), .clk(clk), .tohost(tohost));
  Multiplexer #(.enable("false"), .select(2), .width(32)) multiplexer_6 (
    .in0(PC_n_4), .in1(WRITE_ADDRESS), .in2(READ_DATA), .out(multiplexer_6_out), .sel(control_logic_1_wbsel));  // open: in3

  assign WRITE_ENABLE[2:0] = {3{WRITE_ENABLE[3]}};

  // Other names for the same wires on the sheet: ALURes[31:0] = WRITE_ADDRESS

  // Notes on the sheet:
  //   Output to IMEM
  //   IMEM (do **NOT** move this)
  //   beq t1, t2, good
  //   addi t1, t1, 22
  //   good: addi t1, t1, 222
  //   Inputs from IMEM
  //   Inputs/Outputs for testing. Do **NOT** move these.
  //   Just a bunch of combinational logic
  //   PC
  //   rs1
  //   rs2
  //   imm
  //   Just a bunch of combinational logic
  //   rs1
  //   imm
  //   Outputs To DMEM
  //   DMEM (do **NOT** move this)
  //   Inputs From DMEM
endmodule
